// Logisim project CPU(S-MIPS).circ as structural Verilog: 1 circuit, main circuit S-MIPS
module S_MIPS (
  input  [31:0] RAM_Out_0,
  input  [31:0] RAM_Out_1,
  input  [31:0] RAM_Out_2,
  input  [31:0] RAM_Out_3,
  input  [3:0] Read_Time,
  input  [3:0] Write_Time,
  input  Start,
  input  Clock,
  input  Kbd_Available,
  input  [6:0] Kbd_ASCII_Data,
  output [31:0] RAM_In_0,
  output [31:0] RAM_In_1,
  output [31:0] RAM_In_2,
  output [31:0] RAM_In_3,
  output Halt,
  output [15:0] Address,
  output Kbd_Enable,
  output Kbd_Clear,
  output TTY_Enable,
  output [6:0] TTY_ASCII_Data,
  output [3:0] Mask,
  output nRead_Write,
  output Chip_Select
);

  wire cronoRST, Fetch, Ram_Ready, ReadIns, rnd_kbd, RST;
  wire [2:0] S_FC;
  wire [3:0] ALU_OP;
  wire [5:0] FuncCode, OpCode;
  wire [18:0] SelectorCodes;
  wire [31:0] MemoryAddress, MemoryData, Out_Word;

  // Control_Unit control_unit_1: pin names not known; wires that end beside it: Start, Ram_Ready, FuncCode, OpCode, Clock, RST, cronoRST, Kbd_Enable, S_FC, ALU_OP, SelectorCodes, rnd_kbd, TTY_Enable, ReadIns, Chip_Select, Fetch, nRead_Write, Halt
  Memory_Controller memory_controller_1 (
    .Input_Word(MemoryData), .O0(RAM_Out_0), .O1(RAM_Out_1), .O2(RAM_Out_2), .O3(RAM_Out_3),
    .R_W(nRead_Write), .Chip_Select(Chip_Select), .Read_Time(Read_Time), .Write_Time(Write_Time),
    .Address(Address), .OW_Out_Word(Out_Word), .Mask(Mask), .I0(RAM_In_0), .I1(RAM_In_1), .I2(RAM_In_2),
    .I3(RAM_In_3), .Ram_Ready(Ram_Ready), .MemoryAddress(MemoryAddress), .reset(cronoRST), .clk(Clock),
    .GENERAL_RST(Start));
  // DataPath datapath_1: pin names not known; wires that end beside it: RST, Out_Word, Kbd_ASCII_Data, Kbd_Available, Fetch, ReadIns, SelectorCodes, rnd_kbd, ALU_OP, S_FC, Clock, MemoryAddress, TTY_ASCII_Data, FuncCode, OpCode, MemoryData, Kbd_Clear

  // Other names for the same wires on the sheet: CLK = Clock; CS = Chip_Select; KBD_AVAIL = Kbd_Available;
  //   KBD_CLR = Kbd_Clear; KBD_DATA[6:0] = Kbd_ASCII_Data; RAM_A[15:0] = Address; RAM_MASK[3:0] = Mask;
  //   RI0[31:0] = RAM_In_0; RI1[31:0] = RAM_In_1; RI2[31:0] = RAM_In_2; RI_3[31:0] = RAM_In_3; RO0[31:0] = RAM_Out_0;
  //   RO1[31:0] = RAM_Out_1; RO2[31:0] = RAM_Out_2; RO3[31:0] = RAM_Out_3; RW = nRead_Write;
  //   TTY_DATA[6:0] = TTY_ASCII_Data

  // Notes on the sheet:
  //   RAM TIMING
  //   KEYBOARD
  //   DATA FROM RAM
  //   DATA TO RAM
  //   RAM ADDRESS
  //   KEYBOARD
  //   TTY
  //   DATA WRITE MASK
  //   RAM CONTROL
endmodule
