// Logisim project DataPath.circ as structural Verilog: 1 circuit, main circuit DataPath
module DataPath (
  input  [12:0] Selectors_Code,
  input  [31:0] Instruction,
  input  [6:0] KBD_Data,
  input  KBD_Enable,
  input  fetch,
  input  reset,
  input  S_SI,
  output [31:0] PC_Addrs,
  output [6:0] TTY_Data
);

  wire A____B, A____B_t, A___B_signed, A___B_signed_t, A___B_unsigned, B_Cero, clk, FC, not_1_out, R_Hi_Lo;
  wire [2:0] S_FlagCondition;
  wire [3:0] Op;
  wire [4:0] DA, Rd, Rt, SA, SB;
  wire [15:0] Const;
  wire [25:0] dest;
  wire [31:0] ALU_Out, B, B_prime, bit_extender_2_out, Const_extended, DATA_HI, DATA_HI_LO, DATA_INPUT,
       DATA_LO, Hi, jmp_address, Lo, multiplexer_7_out, NI, random_1_out, Special_Ins_Data;
  wire [31:7] A;

  Multiplexer #(.select(2), .width(5), .enable("false")) multiplexer_1 (
    .in0(Rt), .in1({5{1'b0}}), .out(SB), .sel(Selectors_Code[4:3]));  // open: in2, in3
  Multiplexer #(.select(2), .width(5), .enable("false")) multiplexer_2 (
    .in0(Rd), .in1(Rt), .in2({5{1'b0}}), .out(DA), .sel(Selectors_Code[1:0]));  // open: in3
  Multiplexer #(.select(2), .width(32), .enable("false")) multiplexer_3 (
    .in0(ALU_Out), .in1(Special_Ins_Data), .in2(Lo), .in3(Hi), .out(DATA_INPUT), .sel(Selectors_Code[6:5]));
  Branch_Control branch_control_1 (
    .JS_Jump_Size(Const_extended), .IA_InstructionAddress(PC_Addrs), .jmp(Selectors_Code[10]), .FC(FC),
    .NIR_NextInstructionAddrs(NI));
  ProgramCounter programcounter_1 (
    .jmp_addr(jmp_address), .jmp_Jump(Selectors_Code[10]), .rst_Reset(reset), .Q(PC_Addrs), .fetch(fetch));  // open: clock
  assign Const_extended = {{16{1'b0}}, Const};  // Bit_Extender bit_extender_1
  // InstructionDecoder instructiondecoder_1: pin names not known; wires that end beside it: Instruction, DA, Selectors_Code[2], SA, Rt, Selectors_Code[10], FC, dest, Const, Op
  Multiplexer #(.select(2), .width(32), .enable("false")) multiplexer_4 (
    .in0(B), .in1(Const_extended), .in2({32{1'b0}}), .out(B_prime), .sel(Selectors_Code[8:7]));  // open: in3
  not not_1 (not_1_out, A____B_t);
  RegisterFile registerfile_1 (
    .DA_DestinationAddress(DA), .DI_DataInput(DATA_INPUT), .RW_Read_Write(Selectors_Code[2]),
    .Rst_Reset(reset), .SA(SA), .SB(SB), .Out_A({A, TTY_Data}), .Out_B(B));
  Multiplexer #(.select(3), .enable("false")) multiplexer_5 (
    .in0(1'b0), .in1(A___B_signed), .in2(A___B_unsigned), .in3(A____B), .in4(A___B_signed_t), .in5(A____B_t),
    .in6(not_1_out), .out(FC), .sel(S_FlagCondition));  // open: in7
  Multiplexer #(.select(2), .width(32), .enable("false")) multiplexer_6 (
    .in0(NI), .in1({A, TTY_Data}), .in2({PC_Addrs[31:28], dest, 2'b00}), .out(jmp_address),
    .sel(Selectors_Code[12:11]));  // open: in3
  ALU alu_1 (
    .A({A, TTY_Data}), .B(B_prime), .Op(Op), .HI_CONTENT(DATA_HI), .Output(ALU_Out), .LO_CONTENT(DATA_LO),
    .B_ZERO(B_Cero));  // open: UPDATE_HI_LO, A___B_unsigned, A___B_signed, A____B, A____B_2, A___B_s
  assign bit_extender_2_out = {{25{1'b0}}, KBD_Data};  // Bit_Extender bit_extender_2
  Random #(.width(32)) random_1 (.clk(clk), .next(1'b1), .out(random_1_out), .clr(reset));
  Multiplexer #(.width(32), .enable("false")) multiplexer_7 (
    .in0({32{1'b1}}), .in1(bit_extender_2_out), .out(multiplexer_7_out), .sel(KBD_Enable));
  Hi_Lo_registers_Finished__main main_1 (
    .HI_Content(DATA_HI), .Lo_Content(DATA_LO), .Update(Selectors_Code[9]), .Reset(reset),
    .Read_HI_Lo(R_Hi_Lo), .HI_Lo_Data(DATA_HI_LO));
  Multiplexer #(.width(32), .enable("false")) multiplexer_8 (
    .in0(multiplexer_7_out), .in1(random_1_out), .out(Special_Ins_Data), .sel(S_SI));
  Clock clock_1 (.out(clk));

  // Other names for the same wires on the sheet: A[6:0] = TTY_Data; final_dest[31:2] = {PC_Addrs[31:28], dest};
  //   PC[31:0] = PC_Addrs; Ins[31:0] = Instruction; KBD_Available = KBD_Enable; rst = reset;
  //   S_Special_Instruction = S_SI; S_DA[1:0] = Selectors_Code[1:0]; R_W = Selectors_Code[2];
  //   S_SB[1:0] = Selectors_Code[4:3]; S_DATA_IN[1:0] = Selectors_Code[6:5]; S_ALUB[1:0] = Selectors_Code[8:7];
  //   UpdateHi_Lo = Selectors_Code[9]; Jmp = Selectors_Code[10]; S_jmp_address[1:0] = Selectors_Code[12:11]

  // Notes on the sheet:
  //   Register File
  //   ALU
  //   DATA PATH
  //   MUX ENTRADAS
  //   Branch Contol
  //   Program Counter
  //   Special Instruction Data Input
  //   Inputs
  //   Outputs
endmodule
